// Logisim project logic3.circ as structural Verilog: 1 circuit, main circuit main
module main (
  input  D,
  input  C,
  input  B,
  input  A,
  input  LT,
  input  RBI,
  input  in_7,
  input  in_8,
  input  in_9,
  input  in_10
);

  wire n7447_1_pin9, n7447_1_pin10, n7447_1_pin11, n7447_1_pin12, n7447_1_pin13, n7447_1_pin14,
       n7447_1_pin15, n7447_2_pin3, n7447_2_pin5, n7447_2_pin9, n7447_2_pin10, n7447_2_pin11, n7447_2_pin12,
       n7447_2_pin13, n7447_2_pin14, n7447_2_pin15;

  _7447 #(.ShowInternalStructure("true")) u_7447_1 (
    .pin1(B), .pin2(C), .pin3(LT), .pin5(RBI), .pin6(D), .pin7(A), .pin15(n7447_1_pin15),
    .pin14(n7447_1_pin14), .pin13(n7447_1_pin13), .pin12(n7447_1_pin12), .pin11(n7447_1_pin11),
    .pin10(n7447_1_pin10), .pin9(n7447_1_pin9));  // open: pin4
  _7447 #(.ShowInternalStructure("true")) u_7447_2 (
    .pin1(in_9), .pin2(in_8), .pin3(n7447_2_pin3), .pin5(n7447_2_pin5), .pin6(in_7), .pin7(in_10),
    .pin15(n7447_2_pin15), .pin14(n7447_2_pin14), .pin13(n7447_2_pin13), .pin12(n7447_2_pin12),
    .pin11(n7447_2_pin11), .pin10(n7447_2_pin10), .pin9(n7447_2_pin9));  // open: pin4
  _7_Segment_Display #(.active("false")) u_7_segment_display_1 (
    .g(n7447_1_pin14), .f(n7447_1_pin15), .a(n7447_1_pin13), .b(n7447_1_pin12), .e(n7447_1_pin9),
    .d(n7447_1_pin10), .c(n7447_1_pin11));  // open: dp
  _7_Segment_Display #(.active("false")) u_7_segment_display_2 (
    .g(n7447_2_pin14), .f(n7447_2_pin15), .a(n7447_2_pin13), .b(n7447_2_pin12), .e(n7447_2_pin9),
    .d(n7447_2_pin10), .c(n7447_2_pin11));  // open: dp
  Hex_Digit_Display hex_digit_display_1 (.value({D, C, B, A}));  // open: dp
endmodule
